# Fritzing sketch ColorSoundBoard_v2 (saved by Fritzing 0.9.4)
circuit board: 5.8cm x 7.4cm
breadboards: 1

parts:
  DFRobot_DFPlayer_Mini1 = DFRobot DFPlayer Mini [part_number=DFR0299]
  VCC1 = 4 x AAA Battery Mount  # not connected
  SP1 = SPEAKER [package=pcb_mount_speaker]  # not connected
  R1 = Resistor [tolerance=±5% resistance=10 package=THT]
  Speaker = female pin header, 3 pins [form="♀ (female)"]
  Arduino_Micro = Arduino Micro (Rev3)
  Vol = Trimmer Potentiometer [maximum_resistance=100kΩ package=THT]
  Output = female pin header, 4 pins [form="♀ (female)"]
  Power_5v = female pin header, 2 pins [form="♀ (female)"]
  Power_24v = female pin header, 4 pins [form="♀ (female)"]
  LED = female pin header, 3 pins [form="♀ (female)"]
  Input = female pin header, 4 pins [form="♀ (female)"]
  R8 = Resistor [tolerance=±5% resistance=220 package=THT]
  R9 = Resistor [tolerance=±5% resistance=220 package=THT]
  R7 = Resistor [tolerance=±5% resistance=220 package=THT]
  R6 = Resistor [tolerance=±5% resistance=220 package=THT]
  R10 = Resistor [tolerance=±5% resistance=220 package=THT]
  R3 = Resistor [tolerance=±5% resistance=220 package=THT]
  R4 = Resistor [tolerance=±5% resistance=220 package=THT]
  R5 = Resistor [tolerance=±5% resistance=220 package=THT]
  R11 = Resistor [tolerance=±5% resistance=220 package=THT]
  R12 = Resistor [tolerance=±5% resistance=220 package=THT]
  R13 = Resistor [tolerance=±5% resistance=220 package=THT]
  R14 = Resistor [tolerance=±5% resistance=220 package=THT]

nets:
  VCC: DFRobot_DFPlayer_Mini1.VCC, Arduino_Micro.D9_PWM/A9, Arduino_Micro.5V, Vol.leg2, Output.pin1, R5.Pin_1, R14.Pin_1
  N1: DFRobot_DFPlayer_Mini1.RX, R1.Pin_1
  N2: DFRobot_DFPlayer_Mini1.TX, Arduino_Micro.D10_PWM/A10
  N3: DFRobot_DFPlayer_Mini1.SPK_1, Speaker.pin1
  N4: DFRobot_DFPlayer_Mini1.GND-1, DFRobot_DFPlayer_Mini1.GND-2, Speaker.pin2, Arduino_Micro.GND, Vol.leg1, Power_5v.pin1, R8.Pin_1, R9.Pin_1, R7.Pin_1, R6.Pin_1, R10.Pin_0, R11.Pin_0, R12.Pin_0, R13.Pin_0, R14.Pin_0
  N5: DFRobot_DFPlayer_Mini1.SPK_2, Speaker.pin3
  N6: DFRobot_DFPlayer_Mini1.BUSY, Arduino_Micro.D2/SDA
  N7: R1.Pin_0, Arduino_Micro.D11_PWM
  N8: Arduino_Micro.D4_PWM/A6, Output.pin4, R10.Pin_1, R3.Pin_0, R11.Pin_1
  N9: Arduino_Micro.D5_PWM, LED.pin3
  N10: Arduino_Micro.D6_PWM/A7, Output.pin3, R3.Pin_1, R4.Pin_0, R12.Pin_1
  N11: Arduino_Micro.D8_PWM/A8, Output.pin2, R4.Pin_1, R5.Pin_0, R13.Pin_1
  N12: Arduino_Micro.VIN, Power_5v.pin2
  N13: Arduino_Micro.A5, Vol.wiper
  N14: Arduino_Micro.A3, Input.pin1, R8.Pin_0
  N15: Arduino_Micro.A2, Input.pin2, R9.Pin_0
  N16: Arduino_Micro.A1, Input.pin3, R7.Pin_0
  N17: Arduino_Micro.A0, Input.pin4, R6.Pin_0
  N18: Power_24v.pin1, Power_24v.pin3, LED.pin2
  N19: Power_24v.pin2, Power_24v.pin4, LED.pin1

notes:
  -
  +
